// Digital circuit Assembler.dig as structural Verilog
module Assembler (
  input  mode,
  input  [15:0] value,
  input  [1:0] dest,
  input  [1:0] src,
  input  tworeg,
  input  ADD,
  input  SUB,
  input  MOVE,
  input  JUMP,
  input  AND,
  input  OR,
  input  XOR,
  input  NOT,
  output [31:0] inst,
  output store_clock
);

  wire priorityencoder_1_any;

  PriorityEncoder #(.Selector_Bits(3)) priorityencoder_1 (
    .in0(ADD), .in1(SUB), .in2(AND), .in3(OR), .in4(XOR), .in5(NOT), .in6(MOVE), .in7(JUMP),
    .num(inst[26:24]), .any(priorityencoder_1_any));
  and and_1 (store_clock, priorityencoder_1_any, mode);

  assign {inst[31:27], inst[23:0]} = {4'b0000, tworeg, 2'b00, src, 2'b00, dest, value};

  // Notes on the sheet:
  //   mode: default 100
  //   value: default 100
  //   dest: default 1
  //   src: default 1
  //   tworeg: default 1
endmodule
