// Digital circuit Decoder.dig as structural Verilog
module Decoder (
  input  [31:0] instr,
  input  [15:0] rdval,
  input  [15:0] rsval,
  output [1:0] rs,
  output [1:0] rd,
  output add,
  output [15:0] L,
  output [15:0] R,
  output jump,
  output move,
  output [2:0] mux_out,
  output sub,
  output AND,
  output OR,
  output XOR,
  output NOT
);

  Multiplexer #(.Bits(16)) multiplexer_1 (.sel(instr[27]), .in_0(instr[15:0]), .in_1(rsval), .out(R));
  Decoder #(.Selector_Bits(3)) decoder_1 (
    .sel(instr[26:24]), .out_0(add), .out_1(sub), .out_2(AND), .out_3(OR), .out_4(XOR), .out_5(NOT),
    .out_6(move), .out_7(jump));
  PriorityEncoder #(.Selector_Bits(3)) priorityencoder_1 (
    .in0(jump), .in1(add), .in2(move), .in3(sub), .in4(AND), .in5(OR), .in6(XOR), .in7(NOT), .num(mux_out));  // open: any

  assign L = rdval;
  assign rd = instr[17:16];
  assign rs = instr[21:20];
endmodule
