// Digital circuit Execute.dig as structural Verilog
module Execute (
  input  [2:0] mux_out,
  input  [15:0] L,
  input  [15:0] R,
  output [15:0] result
);

  wire [15:0] add_1_s, and_1_out, not_1_out, or_1_out, sub_1_s, xor_1_out;

  assign xor_1_out = L ^ R;  // XOr xor_1, 16 bits wide
  assign not_1_out = ~R;  // Not not_1, 16 bits wide
  assign or_1_out = L | R;  // Or or_1, 16 bits wide
  Sub #(.Bits(16)) sub_1 (.a(L), .b(R), .c_i(1'b0), .s(sub_1_s));  // open: c_o
  assign and_1_out = L & R;  // And and_1, 16 bits wide
  Add #(.Bits(16)) add_1 (.a(L), .b(R), .c_i(1'b0), .s(add_1_s));  // open: c_o
  Multiplexer #(.Selector_Bits(3), .Bits(16)) multiplexer_1 (
    .sel(mux_out), .in_0(L), .in_1(add_1_s), .in_2(R), .in_3(sub_1_s), .in_4(and_1_out), .in_5(or_1_out),
    .in_6(xor_1_out), .in_7(not_1_out), .out(result));
endmodule
