// Digital circuit FetchUint.dig as structural Verilog
module FetchUint (
  input  prog,
  input  [31:0] bypass,
  input  [31:0] instr_i,
  input  Clock,
  input  [15:0] Value,
  input  Jump,
  output [31:0] inster_0,
  output [3:0] PC
);

  Multiplexer #(.Bits(32)) multiplexer_1 (.sel(prog), .in_0(instr_i), .in_1(bypass), .out(inster_0));
  CounterPreset #(.Bits(4)) counterpreset_1 (
    .en(1'b1), .C(Clock), .dir(1'b0), .in(Value[3:0]), .ld(Jump), .clr(1'b0), .out(PC));  // open: ovf
endmodule
