// Digital circuit Frontpanel.dig as structural Verilog
module Frontpanel (
  input  [15:0] Value,
  input  [1:0] dest,
  input  [1:0] src,
  input  tworeg,
  output [15:0] R0,
  output [15:0] R1,
  output [15:0] R2,
  output [15:0] R3,
  output [1:0] Rd,
  output [15:0] L,
  output [15:0] R,
  output [1:0] Rs,
  output [3:0] PC,
  output [15:0] Target,
  output [1:0] Rs_2,
  output [1:0] Rd_2,
  output [15:0] R_2,
  output [1:0] Rs_3,
  output [1:0] Rd_3,
  output [15:0] L_2,
  output [15:0] R_3,
  output [1:0] Rs_4,
  output [1:0] Rs_5,
  output [1:0] Rd_4,
  output [15:0] L_3,
  output [15:0] R_4,
  output [1:0] Rs_6,
  output [1:0] Rs_7,
  output [1:0] Rd_5,
  output [15:0] L_4,
  output [15:0] R_5,
  output [1:0] Rs_8,
  output [1:0] Rs_9,
  output [1:0] Rd_6,
  output [15:0] R_6,
  output [1:0] Rs_10,
  output [1:0] Rd_7,
  output [15:0] L_5,
  output [15:0] R_7,
  output [1:0] Rs_11,
  output [1:0] Rs_12
);

  wire add, ADD_out, AND, AND_out, assembler_1_store_clock, CLK, dipswitch_1_out, JUMB_out, jump, move,
       MOVE_out, NOT, NOT_out, OR, OR_out, pmshim_1_p6, pmshim_1_p7, pmshim_1_p8, pmshim_1_p9, sub, SUB_out,
       XOR, XOR_out;
  wire [2:0] decoder_1_mux_out;
  wire [3:0] pmshim_1_p4;
  wire [15:0] execute_1_result, register_file_1_rdval, register_file_1_rsval;
  wire [31:0] assembler_1_inst, fetchuint_1_inster_0, pmshim_1_p5, Program_d;

  Button u_ADD (.out(ADD_out));
  Button u_SUB (.out(SUB_out));
  Button u_MOVE (.out(MOVE_out));
  Button JUMB (.out(JUMB_out));
  Button u_AND (.out(AND_out));
  Button u_OR (.out(OR_out));
  Button u_XOR (.out(XOR_out));
  Button u_NOT (.out(NOT_out));
  LED led_1 (.in(dipswitch_1_out));
  DipSwitch dipswitch_1 (.out(dipswitch_1_out));
  Assembler assembler_1 (
    .mode(dipswitch_1_out), .value(Value), .dest(dest), .src(src), .tworeg(tworeg), .ADD(ADD_out),
    .SUB(SUB_out), .MOVE(MOVE_out), .JUMP(JUMB_out), .AND(AND_out), .OR(OR_out), .XOR(XOR_out),
    .NOT(NOT_out), .inst(assembler_1_inst), .store_clock(assembler_1_store_clock));
  // pmshim pmshim_1: pin names not known; wires that end beside it: PC, assembler_1_inst, assembler_1_store_clock, pmshim_1_p4, pmshim_1_p5, pmshim_1_p6, pmshim_1_p7, pmshim_1_p8, pmshim_1_p9
  EEPROMDualPort #(.AddrBits(4), .isProgramMemory("true"), .Bits(32)) Program (
    .A(pmshim_1_p4), .Din(pmshim_1_p5), .str(pmshim_1_p6), .C(pmshim_1_p7), .ld(pmshim_1_p8), .D(Program_d));
  Button button_1 (.out(CLK));
  LED add_2 (.in(add));
  LED add_3 (.in(sub));
  LED move_2 (.in(move));
  LED u_jump (.in(jump));
  FetchUint fetchuint_1 (
    .prog(dipswitch_1_out), .bypass(assembler_1_inst), .instr_i(Program_d), .Clock(CLK), .Value(R),
    .Jump(jump), .inster_0(fetchuint_1_inster_0), .PC(PC));
  Decoder decoder_1 (
    .instr(fetchuint_1_inster_0), .rdval(register_file_1_rdval), .rsval(register_file_1_rsval), .rs(Rs),
    .rd(Rd), .add(add), .L(L), .R(R), .jump(jump), .move(move), .mux_out(decoder_1_mux_out), .sub(sub),
    .AND(AND), .OR(OR), .XOR(XOR), .NOT(NOT));
  Execute execute_1 (.mux_out(decoder_1_mux_out), .L(L), .R(R), .result(execute_1_result));
  LED AND_2 (.in(AND));
  LED OR_2 (.in(OR));
  LED XOR_2 (.in(XOR));
  LED NOT_2 (.in(NOT));
  Register_File register_file_1 (
    .Rs(Rs), .Rd(Rd), .result(execute_1_result), .clock(CLK), .rdval(register_file_1_rdval),
    .rsval(register_file_1_rsval), .R0(R0), .R1(R1), .R2(R2), .R3(R3));

  assign L_2 = L;
  assign L_3 = L;
  assign L_4 = L;
  assign L_5 = L;
  assign R_2 = R;
  assign R_3 = R;
  assign R_4 = R;
  assign R_5 = R;
  assign R_6 = R;
  assign R_7 = R;
  assign Rd_2 = Rd;
  assign Rd_3 = Rd;
  assign Rd_4 = Rd;
  assign Rd_5 = Rd;
  assign Rd_6 = Rd;
  assign Rd_7 = Rd;
  assign Rs_2 = Rd;
  assign Rs_3 = Rs;
  assign Rs_4 = Rs;
  assign Rs_5 = Rd;
  assign Rs_6 = Rs;
  assign Rs_7 = Rd;
  assign Rs_8 = Rs;
  assign Rs_9 = Rd;
  assign Rs_10 = Rs;
  assign Rs_11 = Rs;
  assign Rs_12 = Rd;
  assign Target = R;

  // Other names for the same wires on the sheet: LL[15:0] = L

  // Notes on the sheet:
  //   Programing
  //   Mode
  //   Fibbonacci
  //   0 : MOVE R1 1
  //   1 : MOVE R2 R0
  //   2 : ADD R2 R1
  //   3 : MOVE R0 R1
  //   4 : MOVE R1 R2
  //   5 : JUMP 1
  //   register swap
  //   0 : MOVE R0 5       
  //   1 : MOVE R1 10     
  //   2 : XOR R0 R1   
  //   3 : XOR R1 R0  
  //   4 : XOR R0 R1
  //   sum form 1 to 5
  //   0 : MOVE R0 5       
  //   1 : ADD R1 R0     
  //   2 : SUB R0 1   
  //   3 : JUMP 1
  //   STEP
  //   contents of Program (hex, n*v repeats v):
  //   6000005,8010000,1000001,7000001,c100000,7000001
  //   16 BIT COMPUTER
  //   PC
  //   R
  //   (
  //   =
  //   )
  //   +
  //   -
endmodule
